# Fritzing sketch Projeto_Smart_Room (saved by Fritzing 0.9.10b)
breadboards: 1

parts:
  Part1 = Arduino Uno (Rev3)
  LED1 = LED - 5mm [color="Green (555nm)" current=0.030 package="5 mm [THT]"]
  R1 = Resistor [tolerance=±5% power=0.25 resistance=220 package=THT]
  LED2 = LED - 5mm [color="Red (633nm)" current=0.030 package="5 mm [THT]"]
  R2 = Resistor [tolerance=±5% power=0.25 resistance=220 package=THT]
  HC-SR04_Sensor_1 = HC-SR04 Ultrasonic Distance Sensor
  PART1 = APDS-9960 RGB and Gesture Sensor [part_number=SEN-12787]
  LCD2004-I2C1 = LCD2004-I2C
  LCD2004-I2C2 = LCD2004-I2C
  Part2 = Adafruit TCA9548A
  LED3 = RGB LED - (4 legs) [package="5 mm [THT]"]  # not connected
  LED4 = LEDs [package=led10mm]
  Part3 = IFR520 MOS module [package=THT]
  BAT1 = BC9VPC [package=bc9vpc]

nets:
  N1: Part1.A4/SDA, Part2.INPUTSDA
  N2: Part1.A5/SCL, Part2.INPUTSCL
  N3: Part1.D11_PWM/MOSI, HC-SR04_Sensor_1.TRIG
  N4: Part1.D12/MISO, HC-SR04_Sensor_1.ECHO
  N5: Part1.D2, PART1.INT
  N6: Part1.D4, R2.Pin_1
  N7: Part1.D7, Part3.SIG
  3V3: Part1.3V3, PART1.VCC
  VCC: Part1.5V, HC-SR04_Sensor_1.VCC, Part2.VCC, Part3.VCC
  GND: Part1.GND, LED1.cathode, LED2.cathode, HC-SR04_Sensor_1.GND, Part2.GND, Part3.GND, BAT1.V-
  N8: LED1.anode, R2.Pin_0
  N9: R1.Pin_0, LED2.anode
  N10: PART1.SDA, Part2.0SDA
  N11: PART1.SCL, Part2.0SCL
  N12: LCD2004-I2C1.SDA, Part2.1SDA
  N13: LCD2004-I2C1.SCL, Part2.1SCL
  N14: LCD2004-I2C2.SDA, Part2.2SCL
  N15: LCD2004-I2C2.SCL, Part2.2SDA
  N16: LED4.A, Part3.V+
  N17: LED4.C, Part3.V-
  N18: Part3.VIN, BAT1.V+

custom parts:
  APDS-9960 RGB and Gesture Sensor: Breakout board for the Avago APDS-9960 proximity, light, RGB, and gesture sensors. Please visit www.sparkfun.com to learn more.
  LCD2004-I2C: A standard character display with 4x20 characters. Comes in many colors with LCM2004 IIC attached.
  Adafruit TCA9548A: You just found the perfect I2C sensor, and you want to wire up two or three or more of them to your Arduino when you realize "Uh oh, this chip has a fixed I2C address, and from what I know about I2C, you cannot have two devices with the same address on the same SDA/SCL pins!" Are you out of luck? You would be, if you didn't have this ultra-cool TCA9548A 1-to-8 I2C multiplexer! Finally, a way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
  LEDs: LEDs Standard schematic elements and footprints for 5mm, 3mm, 1206, and 0603 sized LEDs. 5mm - Spark Fun Electronics SKU : COM-00529 (and others)
