# Fritzing sketch Boguinhas (saved by Fritzing 0.9.3b)
breadboards: 1

parts:
  R1 = Resistor [tolerance=±5% resistance=10 package=THT]
  R2 = Photocell (LDR) [package=THT]
  HC-SR04_Sensor_1 = HC-SR04 Ultrasonic Distance Sensor
  R3 = Resistor [tolerance=±5% resistance=220 package="2512 [SMD]"]
  R4 = Resistor [tolerance=±5% resistance=220 package="2512 [SMD]"]
  R5 = Resistor [tolerance=±5% resistance=220 package="2512 [SMD]"]
  R6 = Resistor [tolerance=±5% resistance=220 package="2512 [SMD]"]
  R7 = Resistor [tolerance=±5% resistance=220 package="2512 [SMD]"]
  R8 = Resistor [tolerance=±5% resistance=220 package="2512 [SMD]"]
  M2 = DC Motor  # not connected
  OLED_I2C1 = OLED 128x64 I2C Monochrome Display
  M3 = Getriebemotor  # not connected
  M4 = Getriebemotor  # not connected
  M7 = Humidity and Temperature Sensor DHT11
  R9 = Resistor [tolerance=±5% resistance=220 package="2512 [SMD]"]
  R10 = Resistor [tolerance=±5% resistance=220 package="2512 [SMD]"]
  J1 = Piezo Speaker
  Componente3 = Arduino Mega 2560 (Rev3)
  Componente4 = Adafruit Motor/Stepper/Servo Shield [part_number="Adafruit #1438"]
  VCC1 = Battery block 9V  # not connected
  M8 = Getriebemotor  # not connected
  M9 = Getriebemotor  # not connected
  HC-SR04_Sensor_2 = HC-SR04 Ultrasonic Distance Sensor
  LED1 = LEDs [package=led10mm]
  LED2 = LEDs [package=led10mm]
  LED3 = LEDs [package=led10mm]
  LED4 = LEDs [package=led10mm]
  LED5 = LEDs [package=led10mm]
  LED6 = LEDs [package=led10mm]
  LED7 = LEDs [package=led10mm]
  LED8 = LEDs [package=led10mm]
  J2 = Basic Servo
  Componente5 = Bluetooth HC-05 Macho

nets:
  GND: R1.Pin_0, HC-SR04_Sensor_1.GND, R3.Pin_1, R4.Pin_1, R5.Pin_1, R6.Pin_1, R7.Pin_0, R8.Pin_0, OLED_I2C1.GND, M7.GND, R9.Pin_1, R10.Pin_1, J1.pin1, Componente3.GND, HC-SR04_Sensor_2.GND, Componente5.GND
  N1: R1.Pin_1, R2.pin_0, Componente3.A15
  VCC: R2.pin_1, HC-SR04_Sensor_1.VCC, OLED_I2C1.VDD, M7.Vcc, Componente3.5V, HC-SR04_Sensor_2.VCC, Componente5.VCC
  N2: HC-SR04_Sensor_1.TRIG, Componente3.D39
  N3: HC-SR04_Sensor_1.ECHO, Componente3.D37
  N4: R3.Pin_0, LED8.C
  N5: R4.Pin_0, LED7.C
  N6: R5.Pin_0, LED6.C
  N7: R6.Pin_0, LED5.C
  N8: R7.Pin_1, LED2.C
  N9: R8.Pin_1, LED1.C
  N10: OLED_I2C1.SDA, Componente3.D20/SDA
  N11: OLED_I2C1.SCK, Componente3.D21/SCL
  N12: M7.Data, Componente3.D42
  N13: R9.Pin_0, LED3.C
  N14: R10.Pin_0, LED4.C
  N15: J1.pin2, Componente3.D43
  N16: Componente3.D11_PWM, Componente5.RXD
  N17: Componente3.D10_PWM, Componente5.TXD
  N18: Componente3.D33, HC-SR04_Sensor_2.TRIG
  N19: Componente3.D35, HC-SR04_Sensor_2.ECHO
  N20: Componente3.D46, LED7.A
  N21: Componente3.D47, LED5.A
  N22: Componente3.D48, LED8.A
  N23: Componente3.D49, LED4.A
  N24: Componente3.D50, LED6.A
  N25: Componente3.D51, LED2.A
  N26: Componente3.D52, LED1.A
  N27: Componente3.D53, LED3.A
  GND_2: Componente4.GND, J2.gnd
  +5V: Componente4.+5V, J2.vcc
  N28: Componente4.D9, J2.pulse

custom parts:
  Humidity and Temperature Sensor DHT11: Digital relative humidity & temperature sensor DHT11
  Adafruit Motor/Stepper/Servo Shield: The original Adafruit Motorshield kit is one of our most beloved kits, which is why we decided to make something even better. We have upgraded the shield kit to make the bestest, easiest way to drive DC and Stepper motors. This shield will make quick work of your next robotics project! We kept the ability to drive up to 4 DC motors or 2 stepper motors, but added many improvements: Instead of a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
