# Fritzing sketch Projeto ligações (saved by Fritzing 0.9.3b)
breadboards: 1

parts:
  ZS-042_RTC1 = ZS-042 RTC Module
  Display1 = LCD screen 16x2 IIC [part_number=101290]
  Componente1 = Arduino Uno (Rev3) - ICSP
  Driver2 = 28BYJ-48 Driver Module [part_number=ULN2003 package=THT]
  SM2 = 28BYJ-48 Stepper Motor [part_number=28BYJ-48]
  S1 = Square Pushbutton
  R1 = Resistor [tolerance=±5% resistance=10k package="2512 [SMD]"]

nets:
  GND: ZS-042_RTC1.GND, Display1.GND, Componente1.GND, Driver2.GND, R1.Pin_1
  VCC: ZS-042_RTC1.VCC, Display1.VCC, Componente1.5V, Driver2.Vmotor
  N1: ZS-042_RTC1.SDA, Display1.SDA, Componente1.A4/SDA
  N2: ZS-042_RTC1.SCL, Display1.SCL, Componente1.A5/SCL
  N3: Componente1.D8, Driver2.IN1
  N4: Componente1.D9_PWM, Driver2.IN2
  N5: Componente1.D10_PWM/SS, Driver2.IN3
  N6: Componente1.D11_PWM/MOSI, Driver2.IN4
  N7: Componente1.D7, S1.leg0
  N8: Driver2.blue-pin, SM2.blue-pin
  N9: Driver2.pink-pin, SM2.pink-pin
  N10: Driver2.yellow-pin, SM2.yellow-pin
  N11: Driver2.orange-pin, SM2.orange-pin
  N12: Driver2.red-pin, SM2.red-pin

custom parts:
  LCD screen 16x2 IIC: LCD screen with HD44780 controller enables showing text, symbols, value or anything else that comes from Croduino/Arduino. It is capable of showing 16 symbols in two lines and therefore can be used in many projects that need to send clearly visible and legible output information.. • Color of symbols: White • Backlight: Blue • Dimensions: 80 x 36 x 12 mm • Screen dimensions: 64.5 x 16 mm •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
  28BYJ-48 Driver Module: Generic male header
  28BYJ-48 Stepper Motor: Unipolar Stepper Motor 28BYJ-48 Top coil - pink & orange Bottom coil - blue & yellow Common rail - red Connector pins: blue - pink - yellow - orange - red
