# Fritzing sketch esquemático Final (saved by Fritzing 0.9.3b)
breadboards: 1

parts:
  MH-ET_LIVE_ESP32_DEVKIT1 = MH-ET LIVE ESP32 DEVKIT 38 pins  # not connected
  M1 = DHT11-Grove-Temperature-Sensor_1
  Componente3 = BH1750
  M2 = keystudio esp32 i/o shield
  Componente4 = LCD1602-I2C  # not connected
  Grove1 = Grove OLED 128x96  # not connected
  BMP280_Breakout1 = BMP280 Breakout Board [part_number=BMP280]  # not connected

nets:
  N1: M1.connector0, M2.IO16
  3V3: M1.connector2, M2.3V3, M2.3.3V
  VCC: Componente3.VCC, M2.5V
  GND: Componente3.GND, M2.GND
  N2: Componente3.SCL, M2.IO22
  N3: Componente3.SDA, M2.IO21

custom parts:
  MH-ET LIVE ESP32 DEVKIT 38 pins: http://mh.nodebb.com/topic/2/mh-et-live-esp32-devkit
  BH1750: Light Sensor
  keystudio esp32 i/o shield: The ESP32-IO shield has brought out all the pins of keyestudio ESP32 Core board in the form of 2.54mm pin header. In order to connect other sensors easily, the ESP32-IO shield also has 2 rows of 2.54mm pin headers, powering external sensors/modules with DC 3.3V voltage.
  LCD1602-I2C: A standard character display, usually with 2x16 characters. Comes in many colors with LCM1602 IIC attached.
  BMP280 Breakout Board: This is a breakout board for the Bosch Sensortec BMP280, "an absolute barometric pressure sensor especially designed for mobile applications." The operation range is 300 to 1100 hPa. Supply voltage is 1.2 to 3.6V. Operating temperature range is -40 to +85 °C.
