# Fritzing sketch CarrinhoExploradorComandoBTooth (saved by Fritzing 0.9.3b)
breadboards: 1

parts:
  Componente1 = Arduino Nano (Rev3.0)
  Joystick = Thumb Joystick
  PowerBank = Battery block 9V
  LCD-IC2_SCL-A5_/_SDA-A4 = LCD screen
  Componente2 = Bluetooth HC-05 Macho
  R1 = Resistor [tolerance=±5% resistance=2.2k package=THT]
  R2 = Resistor [tolerance=±5% resistance=1k package=THT]

nets:
  N1: Componente1.D1/TX, Componente2.TXD
  N2: Componente1.D0/RX, R1.Pin_0, R2.Pin_0
  GND: Componente1.GND, Joystick.GND, LCD-IC2_SCL-A5_/_SDA-A4.VSS, Componente2.GND, R1.Pin_1
  N3: Componente1.D12/MISO, PowerBank.+
  VCC: Componente1.5V, Joystick.VCC, LCD-IC2_SCL-A5_/_SDA-A4.VDD, Componente2.VCC, Componente2.Key
  N4: Componente1.A3, Joystick.VERT
  N5: Componente1.A2, Joystick.HORZ
  N6: Componente1.A1, Joystick.SEL
  N7: Componente2.RXD, R2.Pin_1
