# Fritzing sketch Projeto_Esquema (saved by Fritzing 0.9.3b)
breadboards: 1

parts:
  Componente1 = Arduino Mega 2560 (Rev3)
  LED1 = LED - 5mm [color="Red (633nm)" package="5 mm [THT]"]
  LED2 = LED - 5mm [color="Yellow (595nm)" package="5 mm [THT]"]
  LED3 = LED - 5mm [color="Green (570nm)" package="5 mm [THT]"]
  LED4 = LED - 5mm [color="Red (633nm)" package="5 mm [THT]"]
  LED5 = LED - 5mm [color="Green (570nm)" package="5 mm [THT]"]
  J1 = Piezo Speaker
  Componente2 = LCD1602-I2C
  U1 = 7-SEGMENT-DISPLAY [package=7-segment-display]
  S2 = Pushbutton [package="[THT]"]
  R1 = Resistor [tolerance=±5% resistance=220 package=THT]
  R2 = Resistor [tolerance=±5% resistance=220 package=THT]
  R3 = Resistor [tolerance=±5% resistance=220 package=THT]
  R4 = Resistor [tolerance=±5% resistance=220 package=THT]
  R5 = Resistor [tolerance=±5% resistance=220 package=THT]
  R6 = Resistor [tolerance=±5% resistance=220 package=THT]
  R7 = Resistor [tolerance=±5% resistance=10 package=THT]

nets:
  N1: Componente1.D21/SCL, Componente2.SCL
  N2: Componente1.D20/SDA, Componente2.SDA
  N3: Componente1.D13_PWM, J1.pin2
  N4: Componente1.D12_PWM, LED1.anode
  N5: Componente1.D11_PWM, LED2.anode
  N6: Componente1.D10_PWM, LED3.anode
  N7: Componente1.D9_PWM, LED4.anode
  N8: Componente1.D8_PWM, LED5.anode
  5V: Componente1.5V, Componente2.VCC, S2.Pin_1, S2.Pin_2
  GND: Componente1.GND, J1.pin1, Componente2.GND, R1.Pin_0, R2.Pin_0, R3.Pin_0, R4.Pin_0, R5.Pin_1, R6.Pin_0, R7.Pin_0
  N9: Componente1.D2_PWM, S2.Pin_3, S2.Pin_4, R7.Pin_1
  N10: Componente1.D31, U1.G
  N11: Componente1.D33, U1.E
  N12: Componente1.D35, U1.D
  N13: Componente1.D37, U1.G1
  N14: Componente1.D39, U1.DP
  N15: Componente1.D41, U1.G2
  N16: Componente1.D43, U1.A
  N17: LED1.cathode, R1.Pin_1
  N18: LED2.cathode, R3.Pin_1
  N19: LED3.cathode, R4.Pin_1
  N20: LED4.cathode, R5.Pin_0
  N21: LED5.cathode, R6.Pin_1
  N22: U1.C, U1.F, R2.Pin_1

custom parts:
  LCD1602-I2C: A standard character display, usually with 2x16 characters. Comes in many colors with LCM1602 IIC attached.
