# Fritzing sketch inout_control_esquema (saved by Fritzing 0.9.3b)
breadboards: 1

parts:
  Componente1 = Arduino Uno (Rev3)
  LED1 = smd LED [color="Red (633nm)" package="0603 [SMD]"]
  LED2 = smd LED [color="Green (555nm)" package="0603 [SMD]"]
  J1 = Piezo Speaker
  R1 = Resistor [tolerance=±5% resistance=220 package="1206 [SMD]"]
  R2 = Resistor [tolerance=±5% resistance=220 package="1206 [SMD]"]
  hc-sr1 = hc-sr04
  hc-sr2 = hc-sr04
  J2 = Basic Servo
  C1 = Electrolytic Capacitor [capacitance=100μF package="0807 [SMD, electrolytic]"]
  Componente2 = LCD1602-I2C
  S2 = Pushbutton [package="[SMD]"]
  R3 = Resistor [tolerance=±5% resistance=10k package="2512 [SMD]"]

nets:
  N1: Componente1.A4/SDA, Componente2.SCL
  N2: Componente1.A5/SCL, Componente2.SDA
  N3: Componente1.D10_PWM/SS, J2.pulse
  N4: Componente1.D11_PWM/MOSI, J1.pin2
  N5: Componente1.D12/MISO, LED2.anode
  N6: Componente1.D13/SCK, LED1.anode
  N7: Componente1.D2, S2.Pin_1, S2.Pin_2, R3.Pin_1
  N8: Componente1.D4, hc-sr1.Echo
  N9: Componente1.D5_PWM, hc-sr1.Trig
  N10: Componente1.D6_PWM, hc-sr2.Echo
  N11: Componente1.D7, hc-sr2.Trig
  VCC: Componente1.5V, hc-sr1.VCC, hc-sr2.VCC, J2.vcc, C1.+, Componente2.VCC, S2.Pin_3, S2.Pin_4
  GND: Componente1.GND, J1.pin1, R1.Pin_0, R2.Pin_0, hc-sr1.GND, hc-sr2.GND, J2.gnd, C1.-, Componente2.GND, R3.Pin_0
  N12: LED1.cathode, R1.Pin_1
  N13: LED2.cathode, R2.Pin_1

custom parts:
  LCD1602-I2C: A standard character display, usually with 2x16 characters. Comes in many colors with LCM1602 IIC attached.

// code stored in the sketch: Projeto.ino
#define ledPinR 13
#define ledPinG 12

boolean controlo = 0;

void setup() {
  pinMode(ledPinR, OUTPUT);
  pinMode(ledPinG, OUTPUT);
	
}

void loop() {

  if (controlo == 1) {
    digitalWrite(ledPinR, 1);
    digitalWrite(ledPinG, 1);
  }
	delay(1000);
	controlo = !controlo;
}
