# Fritzing sketch ESQUEMAELETRICOPILHAOFINAL (saved by Fritzing 0.9.3b)
breadboards: 1

parts:
  M1 = fc-51 [package=THT]
  Componente1 = Arduino Uno (Rev3) - ICSP
  LED1 = LED - 5mm [color="Green (570nm)" package="5 mm [THT]"]
  LED2 = LED - 5mm [color="Red (633nm)" package="5 mm [THT]"]
  R1 = Resistor [tolerance=±5% resistance=220 package="0805 [SMD]"]
  R2 = Resistor [tolerance=±5% resistance=220 package="0805 [SMD]"]
  Componente2 = HC-SR04
  J1 = Basic Servo

nets:
  N1: M1.pin1, Componente1.D4
  GND: M1.pin2, Componente1.GND, R1.Pin_1, R2.Pin_1, Componente2.Gnd, J1.gnd
  VCC: M1.pin3, Componente1.5V, Componente2.Vcc, J1.vcc
  N2: Componente1.D8, J1.pulse
  N3: Componente1.D9_PWM, Componente2.Echo
  N4: Componente1.D10_PWM/SS, Componente2.Trig
  N5: Componente1.D2, LED2.anode
  N6: Componente1.D3_PWM, LED1.anode
  N7: LED1.cathode, R1.Pin_0
  N8: LED2.cathode, R2.Pin_0

custom parts:
  HC-SR04: HC-SR04 ultrasonic distance sensor
