# Fritzing sketch Esquema (saved by Fritzing 0.9.3b)
breadboards: 1

parts:
  Componente1 = Arduino BT
  Mod1 = KY-032 IR Obstacle Avoidance Sensor Module [package="Breakout board"]
  Componente2 = Bluetooth HC-05 Macho
  M1 = DC Motor
  M2 = DC Motor
  S1 = H-Bridge with L298N
  BAT1 = BC9VPC [package=bc9vpc]
  Mod2 = KY-032 IR Obstacle Avoidance Sensor Module [package="Breakout board"]

nets:
  N1: Componente1.D8, S1.IN2
  N2: Componente1.PWM_D9, S1.IN1
  N3: Componente1.SS/PWM_D10, S1.ENA
  N4: Componente1.A0, Mod1.out, Mod1.EN
  N5: Componente1.A1, Mod2.out
  N6: Componente1.D2, Componente2.TXD
  N7: Componente1.PWM_D3, Componente2.RXD
  N8: Componente1.PWM_D5, S1.ENB
  N9: Componente1.PWM_D6, S1.IN4
  N10: Componente1.RESET_WT11/D7, S1.IN3
  VIN: Componente1.VIN, S1.5V
  GND: Componente1.GND, Mod1.GND, Componente2.GND, S1.GND, BAT1.V-, Mod2.GND
  5V: Componente1.5V, Mod1.+, Componente2.VCC, Mod2.+
  N11: M1.pin_1, S1.M2-02
  N12: M1.pin_2, S1.M2-01
  N13: M2.pin_1, S1.M1-02
  N14: S1.12V, BAT1.V+

custom parts:
  KY-032 IR Obstacle Avoidance Sensor Module: KY-032 Infrared Obstacle Avoidance Sensor. Distance-adjustable, infrared proximity sensor designed for wheeled robots. Also known as AD-032.
  H-Bridge with L298N: h-bridge
