# Fritzing sketch Trabalho_Final_FF (saved by Fritzing 0.9.3b)
breadboards: 1

parts:
  M1 = E18-D80NK_1 [package=THT]
  Componente1 = Arduino Nano (Rev3.0)
  J1 = Basic Servo
  LED1 = LED - 5mm [color="Red (633nm)" package="5 mm [THT]"]
  LED2 = LED - 5mm [color="Green (560nm)" package="5 mm [THT]"]
  R1 = Resistor [tolerance=±5% resistance=220 package="0402 [SMD]"]
  R2 = Resistor [tolerance=±5% resistance=220 package="0402 [SMD]"]
  Componente2 = LCD1602-I2C
  M2 = fc-51 [package=THT]

nets:
  GND: M1.pin1, Componente1.GND, J1.gnd, R1.Pin_0, R2.Pin_0, Componente2.GND, M2.pin2
  5V: M1.pin2, Componente1.5V, J1.vcc, Componente2.VCC, M2.pin3
  D6: M1.pin3, Componente1.D6
  D7: Componente1.D7, M2.pin1
  D8: Componente1.D8, LED1.anode
  D9: Componente1.D9, J1.pulse
  D10: Componente1.D10, LED2.anode
  A5: Componente1.A5, Componente2.SCL
  A4: Componente1.A4, Componente2.SDA
  N1: LED1.cathode, R1.Pin_1
  N2: LED2.cathode, R2.Pin_1

notes:
  Parque de Estacionamento
  Realizado por : Fernando Filipe
  Esquema Elétrico

custom parts:
  E18-D80NK_1: E18-D80NK Proximity Sensor module.
  LCD1602-I2C: A standard character display, usually with 2x16 characters. Comes in many colors with LCM1602 IIC attached.
